# Fritzing sketch schematic (saved by Fritzing 0.9.2b)
breadboards: 1

parts:
  R1 = Photocell (LDR) [package=THT]
  T1 = LM35 Temperature Sensor [package="TO92 [THT]"]
  Part2 = Arduino Uno (Rev3)
  R2 = Resistor [tolerance=±5% resistance=10k package=THT]
  T2 = LM35 Temperature Sensor [package="TO92 [THT]"]

nets:
  N1: R1.pin_0, Part2.A2, R2.Pin_1
  N2: R1.pin_1, T1.+Vs, Part2.5V, T2.+Vs
  N3: T1.Vout, Part2.A1
  GND: T1.GND, Part2.GND, R2.Pin_0, T2.GND
  N4: Part2.A0, T2.Vout
