# Fritzing sketch schematic (saved by Fritzing 0.9.2b)

parts:
  Part1 = Arduino Uno (Rev3)
  J1 = Basic Servo
  LED1 = LED - 3mm [color="White (4500K)" package="3 mm [THT]"]
  LED2 = LED - 3mm [color="Green (560nm)" package="3 mm [THT]"]
  LED3 = LED - 3mm [color="Red (633nm)" package="3 mm [THT]"]
  LED4 = LED - 3mm [color="Yellow (585nm)" package="3 mm [THT]"]
  LED5 = LED - 3mm [color="Orange (620nm)" package="3 mm [THT]"]
  R1 = Resistor [tolerance=±5% resistance=220 package="2512 [SMD]"]
  R2 = Resistor [tolerance=±5% resistance=220 package="2512 [SMD]"]
  R3 = Resistor [tolerance=±5% resistance=220 package="2512 [SMD]"]
  R4 = Resistor [tolerance=±5% resistance=220 package="2512 [SMD]"]
  R5 = Resistor [tolerance=±5% resistance=220 package="2512 [SMD]"]

nets:
  N1: Part1.D8, R1.Pin_1
  N2: Part1.D9_PWM, R2.Pin_1
  N3: Part1.D10_PWM/SS, R3.Pin_1
  N4: Part1.D11_PWM/MOSI, R4.Pin_1
  N5: Part1.D12/MISO, R5.Pin_1
  GND: Part1.GND, J1.gnd, LED1.cathode, LED2.cathode, LED3.cathode, LED4.cathode, LED5.cathode
  N6: Part1.D5_PWM, J1.pulse
  5V: Part1.5V, J1.vcc
